# Fritzing sketch controller (saved by Fritzing 0.9.3b)
breadboards: 1

parts:
  S1 = Pushbutton [package="[SMD]"]  # not connected
  S2 = Pushbutton [package="[SMD]"]  # not connected
  S3 = Pushbutton [package="[SMD]"]  # not connected
  S4 = Pushbutton [package="[SMD]"]  # not connected
  R1 = Resistor [tolerance=±5% resistance=220 package="2010 [SMD]"]
  R2 = Resistor [tolerance=±5% resistance=220 package=THT]
  R3 = Resistor [tolerance=±5% resistance=220 package="2010 [SMD]"]
  R4 = Resistor [tolerance=±5% resistance=220 package="2010 [SMD]"]
  R5 = Resistor [tolerance=±5% resistance=220 package="2010 [SMD]"]
  Part1 = Arduino Uno (Rev3) - ICSP

nets:
  N1: R1.Pin_0, R5.Pin_1, Part1.A0
  N2: R1.Pin_1, R2.Pin_0
  N3: R2.Pin_1, R3.Pin_0
  N4: R3.Pin_1, R4.Pin_0
  N5: R5.Pin_0, Part1.3V3
